# Fritzing sketch SmartPlantSystem (saved by Fritzing 0.9.9b)
breadboards: 1

parts:
  OLED_I2C1 = OLED 128x64 I2C Monochrome Display
  Argon1 = Particle Argon
  SENS1 = SoilWatch 10

nets:
  N1: OLED_I2C1.SDA, Argon1.SDA
  N2: OLED_I2C1.SCK, Argon1.SCL
  VDD: OLED_I2C1.VDD, Argon1.3.3V, SENS1.VCC
  GND: OLED_I2C1.GND, Argon1.GND, SENS1.GND
  N3: Argon1.A0, SENS1.OUT

custom parts:
  Particle Argon: The Argon is a powerful Wi-Fi enabled development board that can act as either a standalone Wi-Fi endpoint or Wi-Fi enabled gateway for Particle Mesh networks. It is based on the Nordic nRF52840 and has built-in battery charging circuitry so it’s easy to connect a Li-Po and deploy your local network in minutes. The Argon is great for connecting existing projects to the Particle Device Cloud or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
  SoilWatch 10: SoilWatch 10 - Capacitive soil moisture sensor
